# Fritzing sketch prototype (saved by Fritzing 0.7.12b)
breadboards: 1

parts:
  Teensy1 = Teensy 2.0
  IC2 = IC, DIP package, 8 pins [chip_label=DS1621]
  J2 = male pin header, 4 pins [form="♂ (male)"]
  X80 = shrouded pin header, 10 pins [form="♂ (shrouded male)"]
  IC3 = ULN2803A [package=THT]

nets:
  N1: Teensy1.GND, IC2.pin4, IC2.pin5, IC2.pin6, IC2.pin7, J2.pin2, IC3.0V
  N2: Teensy1.B0, X80.pin1
  N3: Teensy1.B1, X80.pin2
  N4: Teensy1.D0, IC2.pin2, J2.pin3
  N5: Teensy1.D1, IC2.pin1, J2.pin4
  N6: Teensy1.C7, IC3.In_8
  N7: Teensy1.VCC, IC2.pin8, J2.pin1, X80.pin3, IC3.COM_-_Common
